# Fritzing sketch Smart_Haven (saved by Fritzing 0.9.3b)
breadboards: 2

parts:
  VCC1 = Battery
  VCC2 = Battery
  U1 = LM2596 step down module
  RHT1 = Humidity and Temperature Sensor RHT03
  A1 = Raspberry Pi 5
  Part1 = LCD1602-I2C
  M1 = 1 chan 5v relay module
  U2 = SWITCH-SPST-2 [package=switch-spst-vertical]
  LED4 = LED - 5mm [color="Red (633nm)" package="5 mm [THT]"]
  LED1 = LED - 5mm [color="Red (633nm)" package="5 mm [THT]"]
  LED3 = LED - 5mm [color="Red (633nm)" package="5 mm [THT]"]
  LED2 = LED - 5mm [color="Red (633nm)" package="5 mm [THT]"]
  U3 = LM2596 step down module
  S1 = H-Bridge with L298N
  M2 = DC Motor

nets:
  N1: VCC1.-, VCC2.+
  GND: VCC1.+, U1.IN+, U1.IN-, U1.OUT-, RHT1.GND_2, A1.GND, A1.Fan-GND, Part1.GND, M1.pin_2, U2.P, LED4.cathode, LED1.cathode, LED3.cathode, LED2.cathode, U3.IN+, U3.IN-, U3.OUT-, S1.GND
  N2: VCC2.-, U2.O
  VCC: U1.OUT+, RHT1.Vcc, Part1.VCC, M1.pin_1
  N3: RHT1.Data-signal, A1.GPIO4
  N4: A1.GPIO2, Part1.SDA
  N5: A1.GPIO3, Part1.SCL
  N6: A1.GPIO17, LED2.anode
  N7: A1.GPIO18, M1.pin_3
  N8: A1.GPIO27, LED3.anode
  N9: A1.GPIO22, LED1.anode
  N10: A1.GPIO23, LED4.anode
  N11: A1.GPIO24, S1.IN1
  N12: A1.GPIO25, S1.IN2
  N13: A1.GPIO19, S1.ENA
  N14: U3.OUT+, S1.12V
  N15: S1.M1-01, M2.pin_1
  N16: S1.M1-02, M2.pin_2

custom parts:
  LM2596 step down module: LM2596 DC-DC step down power supply module 3 A.
  Raspberry Pi 5: The RPi5, a faster version of the awesome Raspberry Pi4B ARM Board with 40 pin gpio.
  LCD1602-I2C: A standard character display, usually with 2x16 characters. Comes in many colors with LCM1602 IIC attached.
  1 chan 5v relay module: 1 Channel 5V Relay Module Board Shield with Optocoupler Support High and Low Level Trigger for Arduino.
  H-Bridge with L298N: h-bridge
